# Fritzing sketch meteostation v5 (saved by Fritzing 0.8.7b)
breadboards: 1

parts:
  Часть1 = Arduino Board Ethernet
  LCD1 = LCD screen  # not connected
  J1 = male pin header, 4 pins [form="♂ (male)"]
  RHT1 = Humidity and Temperature Sensor RHT03
  K1 = CO2 sensor [package=PCB]
  R1 = Resistor [tolerance=±5% resistance=10k package=THT]

nets:
  N1: Часть1.D8, K1.TxD_UART
  N2: Часть1.GND, J1.pin1, J1.pin3, RHT1.GND_1, K1.G0
  N3: Часть1.AREF, J1.pin4
  N4: Часть1.D6_PWM, K1.RxD_UART
  N5: Часть1.D7, RHT1.Data-signal, R1.Pin_1
  5V: Часть1.5V, J1.pin2, RHT1.Vcc, K1.G+, R1.Pin_0

custom parts:
  CO2 sensor: A CO2 sensor from CO2Meter - K30. Datasheet http://co2meters.com/Documentation/Datasheets/DS30-01%20-%20K30.pdf Could not make fine PCB and principal. You should make yours if needed.
